# Fritzing sketch wiring_schema (saved by Fritzing 0.9.3b)
breadboards: 1

parts:
  U1 = ESP32S-HiLetgo [part_number=ESP32S-HiLetgo]
  GSM_SIM_GPSR_SMS_SIM900_SIM1 = SIM800L [package=THT]

nets:
  N1: U1.GPIO25, GSM_SIM_GPSR_SMS_SIM900_SIM1.SIM_RXD
  N2: U1.GPIO27, GSM_SIM_GPSR_SMS_SIM900_SIM1.SIM_TXD
  N3: U1.GND, GSM_SIM_GPSR_SMS_SIM900_SIM1.GND#5
  VIN: U1.VIN, GSM_SIM_GPSR_SMS_SIM900_SIM1.5V

custom parts:
  ESP32S-HiLetgo: HiLetgo ESP-WROOM-32 ESP32 ESP-32S Development Board 2.4GHz Dual-Mode WiFi + Bluetooth Dual Cores Microcontroller The ESP32 integrated with Antenna switches, RF Balun, power amplifiers, low-noise amplifiers, filters, and management modules, and the entire solution occupies the least area of PCB. 2.4 GHz Wi-Fi plus Bluetooth dual-mode chip, with TSMC Ultra-low power consumption 40nm technology,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
